# Fritzing sketch servo_scheme (saved by Fritzing 0.9.6b)

parts:
  Mod1 = Raspberry Pi 4B
  J1 = Basic Servo
  CUI-enc1 = AMT103
  Part1 = I2C level shifter bidirectional

nets:
  3V3: Mod1.3V3, CUI-enc1.5V, Part1.LV
  5V: Mod1.5V, J1.vcc, Part1.HV
  GND: Mod1.GND, J1.gnd, CUI-enc1.GND, Part1.GND
  N1: Mod1.GPIO18, Part1.LV1
  N2: Mod1.GPIO23, CUI-enc1.B
  N3: Mod1.GPIO24, CUI-enc1.A
  N4: J1.pulse, Part1.HV1
